# Fritzing sketch lab-reedswitch (saved by Fritzing 0.9.0b)
breadboards: 2

parts:
  Arduino_Uno_R3 = Arduino Uno (Rev3)
  LED1 = LEDs [package=led10mm]
  R1 = Resistor [tolerance=±5% resistance=220 package=THT]
  S1 = Reed switch [package=THT]
  S2 = Reed switch [package=THT]
  LED2 = LEDs [package=led10mm]
  R2 = Resistor [tolerance=±5% resistance=10k package=THT]
  R3 = Resistor [tolerance=±5% resistance=10k package=THT]

nets:
  N1: Arduino_Uno_R3.D9_PWM, R1.Pin_0
  N2: Arduino_Uno_R3.D2, S1.pin_2, R2.Pin_1
  N3: Arduino_Uno_R3.D3_PWM, S2.pin_2, R3.Pin_1
  N4: Arduino_Uno_R3.5V, S1.pin_1, S2.pin_1
  N5: Arduino_Uno_R3.GND, LED1.C, LED2.C, R2.Pin_0, R3.Pin_0
  N6: LED1.A, R1.Pin_1, LED2.A
